// Logisim project Computer.circ as structural Verilog: 3 circuits, main circuit main
module main (
);

  wire and_1_out, and_2_out, and_3_out, and_4_out, and_5_out, dipswitch_1_sw1, dipswitch_2_sw1,
       n7_segment_display_4_p3, n7_segment_display_5_p3, n7_segment_display_12_p3, portio_4_p3, portio_7_p3,
       portio_8_p1, portio_9_p2;

  DipSwitch #(.number(1)) dipswitch_1 (.sw1(dipswitch_1_sw1));
  DipSwitch #(.number(1)) dipswitch_2 (.sw1(dipswitch_2_sw1));
  _7_Segment_Display u_7_segment_display_1 (.f(dipswitch_2_sw1), .e(dipswitch_2_sw1));  // open: g, a, b, d, c, dp
  _7_Segment_Display u_7_segment_display_2 (.f(dipswitch_1_sw1), .e(dipswitch_1_sw1));  // open: g, a, b, d, c, dp
  DipSwitch #(.number(1)) dipswitch_3 (.sw1(dipswitch_1_sw1));
  _7_Segment_Display u_7_segment_display_3 (
    .f(and_1_out), .a(and_1_out), .b(and_1_out), .e(and_1_out), .d(and_1_out), .c(and_1_out), .dp(and_1_out));  // open: g
  and and_1 (and_1_out, dipswitch_1_sw1, dipswitch_2_sw1);
  and and_2 (and_2_out, and_1_out, and_1_out);
  // _7_Segment_Display 7_segment_display_4: pin names not known; wires that end beside it: and_2_out, and_2_out, n7_segment_display_4_p3, n7_segment_display_4_p3, and_2_out
  // PortIO #(.number(1)) portio_1: pin names not known; wires that end beside it: n7_segment_display_4_p3
  LedBar #(.matrixcols(6)) ledbar_1 (
    .led0(and_4_out), .led1(and_4_out), .led2(and_4_out), .led3(and_4_out), .led4(and_4_out), .led5(and_4_out));
  LedBar #(.matrixcols(1)) ledbar_2 (.led0(n7_segment_display_4_p3));
  // _7_Segment_Display 7_segment_display_5: pin names not known; wires that end beside it: and_2_out, and_2_out, n7_segment_display_5_p3, n7_segment_display_5_p3, and_2_out
  // PortIO #(.number(1)) portio_2: pin names not known; wires that end beside it: n7_segment_display_5_p3
  and and_3 (and_3_out, n7_segment_display_5_p3, n7_segment_display_4_p3);
  and and_4 (and_4_out, and_3_out, and_3_out);
  _7_Segment_Display u_7_segment_display_6 (
    .g(and_4_out), .f(and_4_out), .a(and_4_out), .b(and_4_out), .e(and_4_out), .c(and_4_out));  // open: d, dp
  _7_Segment_Display u_7_segment_display_7 (
    .g(and_4_out), .f(and_4_out), .a(and_4_out), .b(and_4_out), .e(and_4_out), .c(and_4_out));  // open: d, dp
  LedBar #(.matrixcols(1)) ledbar_3 (.led0(n7_segment_display_5_p3));
  _7_Segment_Display u_7_segment_display_8 (
    .f(and_3_out), .a(and_3_out), .b(and_3_out), .e(and_3_out), .d(and_3_out), .c(and_3_out));  // open: g, dp
  // PortIO #(.number(1)) portio_3: pin names not known; wires that end beside it: and_2_out, and_3_out
  LED led_1 (.in(and_4_out));
  _7_Segment_Display u_7_segment_display_9 (
    .g(and_4_out), .f(and_4_out), .a(and_4_out), .b(and_4_out), .e(and_4_out), .d(and_4_out), .c(and_4_out));  // open: dp
  _7_Segment_Display u_7_segment_display_10 (
    .f(and_4_out), .a(and_4_out), .e(and_4_out), .d(and_4_out));  // open: g, b, c, dp
  LedBar #(.matrixcols(1)) ledbar_4 (.led0(and_3_out));
  LedBar #(.matrixcols(1)) ledbar_5 (.led0(portio_4_p3));
  _7_Segment_Display u_7_segment_display_11 (
    .f(portio_4_p3), .a(portio_4_p3), .b(portio_4_p3), .e(portio_4_p3), .d(portio_4_p3), .c(portio_4_p3));  // open: g, dp
  // PortIO #(.number(1)) portio_4: pin names not known; wires that end beside it: and_2_out, and_2_out, portio_4_p3
  LedBar #(.matrixcols(6)) ledbar_6 (
    .led0(and_4_out), .led1(and_4_out), .led2(and_4_out), .led3(and_4_out), .led4(and_4_out), .led5(and_4_out));
  LedBar #(.matrixcols(1)) ledbar_7 (.led0(n7_segment_display_12_p3));
  // _7_Segment_Display 7_segment_display_12: pin names not known; wires that end beside it: and_2_out, and_2_out, n7_segment_display_12_p3, n7_segment_display_12_p3, and_2_out
  // PortIO #(.number(1)) portio_5: pin names not known; wires that end beside it: n7_segment_display_12_p3
  and and_5 (and_5_out, n7_segment_display_12_p3, portio_4_p3);
  and and_6 (and_4_out, and_5_out, and_5_out);
  _7_Segment_Display u_7_segment_display_13 (
    .g(and_4_out), .f(and_4_out), .a(and_4_out), .b(and_4_out), .e(and_4_out), .d(and_4_out), .c(and_4_out));  // open: dp
  LedBar #(.matrixcols(1)) ledbar_8 (.led0(and_5_out));
  // _7_Segment_Display 7_segment_display_14: pin names not known; wires that end beside it: and_2_out, and_2_out, and_5_out, and_5_out
  // PortIO #(.number(1)) portio_6: pin names not known; wires that end beside it: and_5_out
  LED led_2 (.in(and_4_out));
  // PortIO #(.number(1)) portio_7: pin names not known; wires that end beside it: and_2_out, and_2_out, portio_7_p3
  LedBar #(.matrixcols(1)) ledbar_9 (.led0(portio_7_p3));
  _7_Segment_Display u_7_segment_display_15 (
    .f(portio_7_p3), .a(portio_7_p3), .b(portio_7_p3), .e(portio_7_p3), .d(portio_7_p3), .c(portio_7_p3));  // open: g, dp
  // PortIO #(.number(1)) portio_8: pin names not known; wires that end beside it: portio_8_p1
  LedBar #(.matrixcols(6)) ledbar_10 (
    .led0(and_4_out), .led1(and_4_out), .led2(and_4_out), .led3(and_4_out), .led4(and_4_out), .led5(and_4_out));
  LedBar #(.matrixcols(1)) ledbar_11 (.led0(portio_8_p1));
  // _7_Segment_Display 7_segment_display_16: pin names not known; wires that end beside it: and_2_out, and_2_out, portio_8_p1, portio_8_p1, and_2_out
  // PortIO #(.number(1)) portio_9: pin names not known; wires that end beside it: and_2_out, portio_9_p2
  and and_7 (portio_9_p2, portio_8_p1, portio_7_p3);
  LED led_3 (.in(and_4_out));
  and and_8 (and_4_out, portio_9_p2, portio_9_p2);
  _7_Segment_Display u_7_segment_display_17 (
    .f(and_4_out), .a(and_4_out), .e(and_4_out), .d(and_4_out));  // open: g, b, c, dp
  LedBar #(.matrixcols(1)) ledbar_12 (.led0(portio_9_p2));
  _7_Segment_Display u_7_segment_display_18 (
    .f(portio_9_p2), .a(portio_9_p2), .b(portio_9_p2), .e(portio_9_p2), .d(portio_9_p2), .c(portio_9_p2));  // open: g, dp

  // Notes on the sheet:
  //   C
  //   NOTE:
  //   P
  //   DISPLAY: 40x20
  //   1. - On
  //   0. - On
  //   Nothing - Off
  //   N1
  //   N1
  //   SECTOR 1
  //   N0
  //   N0
  //   N1
  //   SECTOR 2
  //   N1
  //   N0
  //   SECTOR 3
  //   N1
  //   N0
endmodule

module learning (
);

  wire button_1_out, button_2_out, dipswitch_1_p1, not_1_out, xor_1_out;

  Button button_1 (.out(button_1_out));
  Button #(.press("passive")) button_2 (.out(button_2_out));
  // DipSwitch #(.number(1)) dipswitch_1: pin names not known; wires that end beside it: dipswitch_1_p1
  not not_1 (not_1_out, button_1_out);
  LED led_1 (.in(not_1_out));
  xor xor_1 (xor_1_out, button_2_out, dipswitch_1_p1);
  LED led_2 (.in(xor_1_out));
endmodule

module Teniac (
);

  wire and_1_out, and_2_out, and_3_out, dipswitch_1_p1, dipswitch_1_p2, undriven;

  // DipSwitch #(.number(2)) dipswitch_1: pin names not known; wires that end beside it: dipswitch_1_p1, dipswitch_1_p2
  LED led_1 (.in(dipswitch_1_p2));
  LED led_2 (.in(dipswitch_1_p1));
  and and_1 (and_1_out, dipswitch_1_p2, dipswitch_1_p1);
  LED led_3 (.in(and_1_out));
  and and_2 (and_2_out, dipswitch_1_p2, dipswitch_1_p1);
  LED led_4 (.in(and_2_out));
  LED led_5 (.in(and_2_out));
  LED led_6 (.in(and_3_out));
  _7_Segment_Display u_7_segment_display_1 (
    .f(and_2_out), .a(and_2_out), .b(and_2_out), .e(and_2_out), .d(and_2_out), .c(and_2_out));  // open: g, dp
  _7_Segment_Display u_7_segment_display_2 (
    .f(and_2_out), .a(and_2_out), .b(and_2_out), .e(and_2_out), .d(and_2_out), .c(and_2_out));  // open: g, dp
  and and_3 (and_3_out, and_2_out, and_2_out);
  LED led_7 (.in(and_2_out));
  _7_Segment_Display u_7_segment_display_3 (
    .f(and_3_out), .a(and_3_out), .b(and_3_out), .e(and_3_out), .d(and_3_out), .c(and_3_out));  // open: g, dp
  LED led_8 (.in(and_3_out));
  LED led_9 (.in(undriven));
  _7_Segment_Display u_7_segment_display_4 (
    .g(undriven), .f(undriven), .a(undriven), .b(undriven), .e(undriven), .c(undriven));  // open: d, dp
  // PortIO #(.number(1)) portio_1: pin names not known; wires that end beside it: and_3_out, and_3_out
  _7_Segment_Display u_7_segment_display_5 ();  // open: g, f, a, b, e, d, c, dp
  _7_Segment_Display u_7_segment_display_6 ();  // open: g, f, a, b, e, d, c, dp
  _7_Segment_Display u_7_segment_display_7 ();  // open: g, f, a, b, e, d, c, dp
  _7_Segment_Display u_7_segment_display_8 ();  // open: g, f, a, b, e, d, c, dp
  _7_Segment_Display u_7_segment_display_9 ();  // open: g, f, a, b, e, d, c, dp
endmodule
